# Fritzing sketch gro-controler (saved by Fritzing 0.9.0b)
circuit board: 8.46667cm x 5.64444cm
breadboards: 1

parts:
  Part1 = Spark Core (v1.0)
  RHT1 = Humidity and Temperature Sensor RHT03
  R1 = Resistor [tolerance=±5% resistance=10k package=THT]
  Part2 = RHT03

nets:
  GND: Part1.GND, RHT1.GND_2, Part2.GND
  N1: Part1.D0, Part2.SCL
  N2: Part1.D2, RHT1.Data-signal, R1.Pin_1
  3V3: Part1.3V3, RHT1.Vcc, R1.Pin_0, Part2.3V3

custom parts:
  RHT03: The RHT03 (also known by DHT-22) is a low cost humidity and temperature sensor with a single wire digital interface. The sensor is calibrated and doesn’t require extra components so you can get right to measuring relative humidity and temperature.
